# Fritzing sketch 06_one_dynamixel (saved by Fritzing 1.0.1rc)
breadboards: 1

parts:
  Mod1 = Raspberry Pi Pico
  S1 = Pushbutton [package="[THT]"]
  IC1 = DIP - 8 pins [chip_label=IC package="DIP (Dual Inline) [THT]"]
  J1 = Basic Servo

nets:
  N1: Mod1.pin_3, Mod1.pin_8, Mod1.pin_13, Mod1.pin_18, Mod1.pin_23, Mod1.pin_28, Mod1.pin_33, Mod1.pin_38, Mod1.pin_42, IC1.J1-4, IC1.J2-4, J1.gnd
  N2: Mod1.pin_16, IC1.J1-3
  N3: Mod1.pin_17, IC1.J1-2
  N4: Mod1.pin_21, S1.Pin_3, S1.Pin_4
  N5: Mod1.pin_36, S1.Pin_1, S1.Pin_2
  N6: Mod1.pin_40, J1.vcc
  N7: IC1.J2-3, J1.pulse

notes:
  GP16 : pull down
  Dynamixel
  (yellow：data)

custom parts:
  Raspberry Pi Pico: Raspberry Pi Pico. Based around the RP2040 microcontroller the Pico is a low cost microcontroller device bringing Raspberry Pi quality, cost, and easy of use to the microcontroller space. Jan 2021, Split part in to two versions: tht (this one) and SMD. This one will drill holes for a .1 in header in pcb to allow plugging in the module as well as providing pads to solder the module to the top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
  DIP - 8 pins: A DIP stand-in part for whatever IC you want. With 8 pins on a 300mil dual inline package (DIP) footprint.
